# Fritzing sketch Sensor (saved by Fritzing 0.9.3b)
breadboards: 1

parts:
  Raspberry_Pi1 = Raspberry Pi 2
  R1 = Resistor [tolerance=±5% resistance=1k package="2010 [SMD]"]
  R2 = Resistor [tolerance=±5% resistance=2.2k package="2010 [SMD]"]
  hc-sr1 = hc-sr04

nets:
  N1: Raspberry_Pi1.GPIO26, R1.Pin_1, R2.Pin_0
  N2: Raspberry_Pi1.GPIO20, hc-sr1.Trig
  GND: Raspberry_Pi1.GND, R2.Pin_1, hc-sr1.GND
  5V: Raspberry_Pi1.5V, hc-sr1.VCC
  N3: R1.Pin_0, hc-sr1.Echo
